// Logisim project adder.circ as structural Verilog: 1 circuit, main circuit main
module main (
  input  Input_A,
  input  sel__A,
  input  in_3,
  input  in_4,
  input  sel__B,
  input  in_6,
  input  Input_B,
  input  in_8,
  input  in_9,
  input  in_10,
  output out_11,
  output out_12,
  output out_13,
  output out_14,
  output out_15
);

  wire adder_1_cout, adder_2_cout, adder_3_cout, xor_1_out, xor_2_out, xor_3_out, xor_4_out;

  xor xor_1 (xor_1_out, sel__B, Input_B);
  xor xor_2 (xor_2_out, sel__B, in_8);
  xor xor_3 (xor_3_out, sel__B, in_9);
  xor xor_4 (xor_4_out, sel__B, in_10);
  Adder #(.width(1)) adder_1 (.a(Input_A), .b(xor_1_out), .out(out_11), .cin(sel__A), .cout(adder_1_cout));
  Adder #(.width(1)) adder_2 (.a(in_3), .b(xor_2_out), .out(out_12), .cin(adder_1_cout), .cout(adder_2_cout));
  Adder #(.width(1)) adder_3 (.a(in_4), .b(xor_3_out), .out(out_13), .cin(adder_2_cout), .cout(adder_3_cout));
  Adder #(.width(1)) adder_4 (.a(in_6), .b(xor_4_out), .out(out_14), .cin(adder_3_cout), .cout(out_15));
endmodule
