// Logisim project bitSelector.circ as structural Verilog: 1 circuit, main circuit main
module main (
  input  [7:0] in_1,
  input  [1:0] in_2,
  output [1:0] out_3
);

  BitSelector #(.group(2)) bitselector_1 (.in(in_1), .out(out_3), .sel(in_2));
endmodule
