// Logisim project decadeCounterfelipefelopi.circ as structural Verilog: 1 circuit, main circuit main
module main (
  input  in_1,
  output out_2,
  output out_3,
  output out_4,
  output out_5
);

  wire and_1_out, clock_1_out, j_k_ff_1_qn, j_k_ff_2_qn, j_k_ff_3_qn, not_1_out;

  not not_1 (not_1_out, clock_1_out);
  Clock clock_1 (.out(clock_1_out));
  J_K_Flip_Flop j_k_ff_1 (
    .J(in_1), .clk(not_1_out), .K(in_1), .Q(out_2), .Qn(j_k_ff_1_qn), .reset(and_1_out));  // open: preset, en
  J_K_Flip_Flop j_k_ff_2 (
    .J(j_k_ff_1_qn), .clk(j_k_ff_1_qn), .K(j_k_ff_1_qn), .Q(out_3), .Qn(j_k_ff_2_qn), .reset(and_1_out));  // open: preset, en
  J_K_Flip_Flop j_k_ff_3 (
    .J(j_k_ff_2_qn), .clk(j_k_ff_2_qn), .K(j_k_ff_2_qn), .Q(out_4), .Qn(j_k_ff_3_qn), .reset(and_1_out));  // open: preset, en
  J_K_Flip_Flop j_k_ff_4 (
    .J(j_k_ff_3_qn), .clk(j_k_ff_3_qn), .K(j_k_ff_3_qn), .Q(out_5), .reset(and_1_out));  // open: Qn, preset, en
  and and_1 (and_1_out, j_k_ff_1_qn, out_3, out_5);
endmodule
