// Logisim project priorityEncoder.circ as structural Verilog: 1 circuit, main circuit main
module main (
  input  in_1,
  input  in_2,
  input  in_3,
  input  in_4,
  input  in_5,
  input  in_6,
  input  in_7,
  input  in_8,
  input  in_9,
  output [2:0] out_10,
  output out_11
);

  Priority_Encoder priority_encoder_1 (
    .in0(in_1), .in1(in_2), .in2(in_3), .in3(in_4), .in4(in_5), .in5(in_6), .in6(in_7), .in7(in_8),
    .out(out_10), .en_in(in_9), .gs(out_11));  // open: en_out
endmodule
