// Logisim project trabCD.circ as structural Verilog: 1 circuit, main circuit main
module main (
  input  Decrement,
  input  [9:0] in_2,
  input  Resert,
  input  Increment,
  input  in_5,
  input  read___0_write__1,
  output [5:0] Braille_Dot
);

  wire clock_1_out, controlled_buffer_1_out, counter_1_carry, not_1_out, not_2_out, not_3_out;
  wire [1:0] bitselector_1_out, bitselector_2_out, bitselector_3_out;
  wire [5:0] rom_1_data;
  wire [9:0] counter_1_q;

  Counter #(.width(10), .max('h3ff)) counter_1 (
    .load(Decrement), .D(in_2), .count(Increment), .Q(counter_1_q), .carry(counter_1_carry),
    .clk(controlled_buffer_1_out), .clr(Resert));
  assign controlled_buffer_1_out = not_1_out ? clock_1_out : 1'bz;  // Controlled_Buffer controlled_buffer_1
  not not_1 (not_1_out, counter_1_carry);
  Clock clock_1 (.out(clock_1_out));
  not not_2 (not_2_out, Resert);
  ROM #(.addrWidth(10), .dataWidth(6)) rom_1 (.addr(counter_1_q), .data(rom_1_data), .sel(in_5));
  not not_3 (not_3_out, read___0_write__1);
  assign Braille_Dot = read___0_write__1 ? rom_1_data : 6'bz;  // Controlled_Buffer controlled_buffer_2
  BitSelector #(.width(6), .group(2)) bitselector_1 (.in(rom_1_data), .out(bitselector_1_out), .sel(2'b10));
  DotMatrix #(.inputtype("row"), .matrixcols(2), .matrixrows(3), .dotshape("circle")) dotmatrix_1 (
    .row0(bitselector_1_out), .row1(bitselector_2_out), .row2(bitselector_3_out));
  BitSelector #(.width(6), .group(2)) bitselector_2 (.in(rom_1_data), .out(bitselector_2_out), .sel(2'b01));
  BitSelector #(.width(6), .group(2)) bitselector_3 (.in(rom_1_data), .out(bitselector_3_out), .sel(2'b00));
  RAM #(.addrWidth(10), .dataWidth(6)) ram_1 (
    .addr(counter_1_q), .data(Braille_Dot), .sel(not_2_out), .clk(clock_1_out), .ld(not_3_out));  // open: clr

  // Notes on the sheet:
  //   contents of rom_1 (hex, n*v repeats v):
  //   18 22 1c 20 1a 2a 24 2e 18 2b 1c 20 36 2e 2a 2b 18 22 1c 20 3c 28 2e 1a 34 1e 2c 1a 2e 1e 36 28 34
  //   1a 2e 38 1e 36 2c 1a 38 1e 3c 36 1a 2e 1e 2c 20 18 22 1c 20 1a 2a 24 2e 18 2b 1c 20 36 2e 2a 2b 18
  //   22 1c 20 3c 28 2e 1a 34 1e 2c 1a 2e 1e 36 28 34 1a 2e 38 1e 36 2c 1a 38 1e 3c 36 1a 2e 1e 2c 20 18
  //   22 1c 20 1a 2a 24 2e 18 2b 1c 20 36 2e 2a 2b 18 22 1c 20 3c 28 2e 1a 34 1e 2c 1a 2e 1e 36 28 34 1a
  //   2e 38 1e 36 2c 1a 38 1e 3c 36 1a 2e 1e 2c 20 18 22 1c 20 1a 2a 24 2e 18 2b 1c 20 36 2e 2a 2b 18 22
  //   1c 20 3c 28 2e 1a 34 1e 2c 1a 2e 1e 36 28 34 1a 2e 38 1e 36 2c 1a 38 1e 3c 36 1a 2e 1e 2c 20 18 22
  //   1c 20 1a 2a 24 2e 18 2b 1c 20 36 2e 2a 2b 18 22 1c 20 3c 28 2e 1a 34 1e 2c 1a 2e 1e 36 28 34 1a 2e
  //   38 1e 36 2c 1a 38 1e 3c 36 1a 2e 1e 2c 20 18 22 1c 20 1a 2a 24 2e 18 2b 1c 20 36 2e 2a 2b 18 22 1c
  //   20 3c 28 2e 1a 34 1e 2c 1a 2e 1e 36 28 34 1a 2e 38 1e 36 2c 1a 38 1e 3c 36 1a 2e 1e 2c 20 18 22 1c
  //   20 1a 2a 24 2e 18 2b 1c 20 36 2e 2a 2b 18 22 1c 20 3c 28 2e 1a 34 1e 2c 1a 2e 1e 36 28 34 1a 2e 38
  //   1e 36 2c 1a 38 1e 3c 36 1a 2e 1e 2c 20 18 22 1c 20 1a 2a 24 2e 18 2b 1c 20 36 2e 2a 2b 18 22 1c 20
  //   3c 28 2e 1a 34 1e 2c 1a 2e 1e 36 28 34 1a 2e 38 1e 36 2c 1a 38 1e 3c 36 1a 2e 1e 2c 20
endmodule
