// Logisim project adder.circ as structural Verilog: 1 circuit, main circuit main
module main (
  input  Input_A,
  input  in_2,
  input  in_3,
  input  in_4,
  input  sel__2,
  input  sel__1,
  input  in_7,
  input  in_8,
  input  Input_B,
  input  in_10,
  output out_11,
  output out_12,
  output out_13,
  output out_14,
  output out_15
);

  wire adder_1_cout, adder_2_cout, adder_3_cout, xor_1_out, xor_2_out, xor_3_out, xor_4_out;

  xor xor_1 (xor_1_out, sel__2, in_7);
  xor xor_2 (xor_2_out, sel__2, in_10);
  xor xor_3 (xor_3_out, sel__2, Input_B);
  xor xor_4 (xor_4_out, sel__2, in_8);
  Adder #(.width(1)) adder_1 (.a(in_4), .b(xor_1_out), .out(out_11), .cin(sel__1), .cout(adder_1_cout));
  Adder #(.width(1)) adder_2 (.a(Input_A), .b(xor_2_out), .out(out_12), .cin(adder_1_cout), .cout(adder_2_cout));
  Adder #(.width(1)) adder_3 (.a(in_3), .b(xor_3_out), .out(out_13), .cin(adder_2_cout), .cout(adder_3_cout));
  Adder #(.width(1)) adder_4 (.a(in_2), .b(xor_4_out), .out(out_14), .cin(adder_3_cout), .cout(out_15));
endmodule
