// Logisim project inverso.circ as structural Verilog
module A (
  input  L1,
  input  L2,
  input  L3,
  input  L4,
  input  L5,
  input  L6,
  output A
);

  or or_1 (A, L2, L1);
endmodule

module C (
  input  L1,
  input  L2,
  input  L3,
  input  L4,
  input  L5,
  input  L6,
  output S
);

  wire and_1_out, and_2_out;

  and and_1 (and_1_out, L3, L4, L5);
  and and_2 (and_2_out, L2, L3, L5);
  or or_1 (S, L6, and_1_out, and_2_out);
endmodule

module D (
  input  L1,
  input  L2,
  input  L3,
  input  L4,
  input  L5,
  input  L6,
  output S
);

  wire and_1_out, and_2_out, and_3_out, and_4_out, and_5_out, not_1_out, not_2_out, not_3_out, not_4_out,
       not_5_out, not_6_out, not_7_out, not_8_out, not_9_out, not_10_out;

  not not_1 (not_1_out, L2);
  not not_2 (not_2_out, L4);
  not not_3 (not_3_out, L6);
  not not_4 (not_4_out, L3);
  not not_5 (not_5_out, L2);
  not not_6 (not_6_out, L5);
  not not_7 (not_7_out, L1);
  not not_8 (not_8_out, L5);
  not not_9 (not_9_out, L6);
  not not_10 (not_10_out, L3);
  and and_1 (and_1_out, not_1_out, not_2_out, L5, not_3_out);
  and and_2 (and_2_out, not_4_out, L4, L5);
  and and_3 (and_3_out, not_5_out, L3, L4, not_6_out);
  and and_4 (and_4_out, not_7_out, L2, not_8_out, not_9_out);
  and and_5 (and_5_out, L2, not_10_out, L5);
  or or_1 (S, and_1_out, and_2_out, and_3_out, and_4_out, and_5_out);
endmodule

module E (
  input  L1,
  input  L2,
  input  L3,
  input  L4,
  input  L5,
  input  L6,
  input  in_7,
  input  in_8,
  input  in_9,
  input  in_10,
  input  in_11,
  input  in_12,
  input  in_13,
  input  in_14,
  output S,
  output out_16,
  output out_17,
  output [5:0] out_18
);

  wire and_1_out, and_2_out, and_3_out, and_4_out, and_5_out, and_6_out, and_7_out, not_1_out, not_2_out,
       not_3_out, not_4_out, not_5_out, not_6_out, not_7_out, not_8_out, not_9_out, not_10_out, not_11_out;
  wire [5:1] undriven;

  not not_1 (not_1_out, L2);
  not not_2 (not_2_out, L4);
  not not_3 (not_3_out, L5);
  not not_4 (not_4_out, L3);
  not not_5 (not_5_out, L6);
  not not_6 (not_6_out, L1);
  not not_7 (not_7_out, L2);
  not not_8 (not_8_out, L4);
  not not_9 (not_9_out, L3);
  not not_10 (not_10_out, L6);
  not not_11 (not_11_out, L5);
  and and_1 (and_1_out, not_1_out, not_2_out, L6);
  and and_2 (and_2_out, not_3_out, L6);
  and and_3 (and_3_out, not_4_out, L4, not_5_out);
  and and_4 (and_4_out, not_6_out, L4, L5);
  and and_5 (and_5_out, not_7_out, L3, not_8_out, L5);
  and and_6 (and_6_out, L2, not_9_out, L5, not_10_out);
  and and_7 (and_7_out, L1, L2, L3, not_11_out);
  or or_1 (S, and_1_out, and_2_out, and_3_out, and_4_out, and_5_out, and_6_out, and_7_out);
  Decoder decoder_1 (.out0(out_16), .out1(out_17), .sel(in_7), .en(in_8));
  BitSelector #(.width(6), .group(6)) bitselector_1 (.in({undriven, in_9}), .out(out_18));  // open: sel
  // Pins of 1 and 6 bits meet at {undriven, in_9}

  assign in_13 = in_10;
  assign in_14 = in_10;
endmodule

module F (
  input  L1,
  input  L2,
  input  L3,
  input  L4,
  input  L5,
  input  L6,
  output S
);

  wire and_1_out, and_2_out, and_3_out, and_4_out, and_5_out, and_6_out, and_7_out, and_8_out, not_1_out,
       not_2_out, not_3_out, not_4_out, not_5_out, not_6_out, not_7_out, not_8_out, not_9_out, not_10_out,
       not_11_out, not_12_out, not_13_out, not_14_out;

  not not_1 (not_1_out, L1);
  not not_2 (not_2_out, L4);
  not not_3 (not_3_out, L2);
  not not_4 (not_4_out, L3);
  not not_5 (not_5_out, L6);
  not not_6 (not_6_out, L2);
  not not_7 (not_7_out, L3);
  not not_8 (not_8_out, L6);
  not not_9 (not_9_out, L2);
  not not_10 (not_10_out, L4);
  not not_11 (not_11_out, L5);
  not not_12 (not_12_out, L5);
  not not_13 (not_13_out, L4);
  not not_14 (not_14_out, L5);
  and and_1 (and_1_out, not_1_out, not_2_out, L5);
  and and_2 (and_2_out, not_3_out, not_4_out, L5, not_5_out);
  and and_3 (and_3_out, not_6_out, L4, L5);
  and and_4 (and_4_out, not_7_out, L4, L5, not_8_out);
  and and_5 (and_5_out, not_9_out, L3, not_10_out, not_11_out);
  and and_6 (and_6_out, L3, L6);
  and and_7 (and_7_out, L2, L3, L4, not_12_out);
  and and_8 (and_8_out, L1, L2, not_13_out, not_14_out);
  or or_1 (S, and_1_out, and_2_out, and_3_out, and_4_out, and_5_out, and_6_out, and_7_out, and_8_out);
endmodule
