// Logisim project LUT.circ as structural Verilog: 1 circuit, main circuit main
module main (
  input  \Configuração_da_LUT ,
  input  in_2,
  input  in_3,
  input  in_4,
  input  in_5,
  input  in_6,
  input  in_7,
  input  in_8,
  input  in_9,
  input  in_10,
  input  in_11,
  input  in_12,
  input  [3:0] Entrada_da_LUT,
  input  in_14,
  input  in_15,
  input  in_16,
  input  in_17,
  input  in_18,
  input  in_19,
  input  in_20,
  output out_21
);

  wire clock_1_out, multiplexer_1_out;

  Clock clock_1 (.out(clock_1_out));
  Multiplexer #(.select(4)) multiplexer_1 (
    .in0(\Configuração_da_LUT ), .in1(in_2), .in2(in_3), .in3(in_4), .in4(in_5), .in5(in_6), .in6(in_7),
    .in7(in_9), .in8(in_11), .in9(in_14), .in10(in_15), .in11(in_16), .in12(in_17), .in13(in_18),
    .in14(in_19), .in15(in_20), .out(multiplexer_1_out), .sel(Entrada_da_LUT), .en(in_12));
  D_Flip_Flop d_ff_1 (
    .clk(clock_1_out), .D(multiplexer_1_out), .Q(out_21), .preset(in_8), .en(in_10), .reset(in_8));  // open: Qn
endmodule
