// Logisim project decoderANDS.circ as structural Verilog: 1 circuit, main circuit main
module main (
  input  A0,
  input  A1,
  output S0,
  output S1,
  output S2,
  output S3
);

  wire not_1_out, not_2_out;

  not not_1 (not_1_out, A0);
  not not_2 (not_2_out, A1);
  and and_1 (S0, not_1_out, not_2_out);
  and and_2 (S1, not_1_out, A1);
  and and_3 (S2, A0, not_2_out);
  and and_4 (S3, A1, A0);
endmodule
